# Fritzing sketch keypad (saved by Fritzing 1.0.4)
circuit board: 7.38197cm x 6.58806cm
breadboards: 1

parts:
  Keypad4x4 = Keypad Membran 4x4
  ESP32-S3 = FireBeetle ESP32-E

nets:
  N1: Keypad4x4.row1, ESP32-S3.pin_8
  N2: Keypad4x4.row2, ESP32-S3.pin_7
  N3: Keypad4x4.row3, ESP32-S3.pin_6
  N4: Keypad4x4.row4, ESP32-S3.pin_5
  N5: Keypad4x4.col1, ESP32-S3.pin_4
  N6: Keypad4x4.col2, ESP32-S3.pin_3
  N7: Keypad4x4.col3, ESP32-S3.pin_2
  N8: Keypad4x4.col4, ESP32-S3.pin_1

custom parts:
  Keypad Membran 4x4: Membrane Keypad 4x4 Matrix
  FireBeetle ESP32-E: FireBeetle ESP32-E, specially designed for IoT, is an ESP-WROOM-32E-based main controller board with dual-core chips. It supports WiFi and Bluetooth dual-mode communication and features a small size, ultra-low power consumption, on-board charging circuit, and easy-to-use interface, which can be conveniently used for smart home IoT, industrial IoT applications, wearable devices, and so on. You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
